// Logisim project LAB-R.circ as structural Verilog: 1 circuit, main circuit main
module main (
  input  [7:0] in_1,
  input  [3:0] in_2,
  input  in_3,
  input  [3:0] in_4,
  input  in_5,
  input  in_6,
  output [7:0] out_7
);

  wire clock_1_out, decoder_1_out0, decoder_1_out1, not_1_out;

  Clock clock_1 (.out(clock_1_out));
  Decoder decoder_1 (.out0(decoder_1_out0), .out1(decoder_1_out1), .sel(in_6), .en(in_5));
  assign out_7 = in_3 ? in_1 : 8'bz;  // Controlled_Buffer controlled_buffer_1
  not not_1 (not_1_out, in_3);
  RAM #(.addrWidth(4)) ram_1 (
    .addr(in_2), .data(out_7), .sel(decoder_1_out0), .clk(clock_1_out), .ld(not_1_out));  // open: clr
  ROM #(.addrWidth(4)) rom_1 (.addr(in_4), .data(out_7), .sel(decoder_1_out1));
endmodule
