// Logisim project LAB-R1.circ as structural Verilog: 1 circuit, main circuit main
module main (
  input  in_1,
  input  [7:0] in_2,
  input  in_3,
  input  in_4,
  input  in_5,
  input  in_6,
  input  [7:0] in_7,
  input  in_8,
  input  in_9,
  input  in_10,
  output [7:0] out_11
);

  wire clock_1_out, counter_1_carry, counter_2_carry, decoder_1_out0, decoder_1_out1, not_1_out;
  wire [6:0] bit_extender_1_out, bit_extender_2_out;
  wire [7:0] counter_1_q, counter_2_q;

  Decoder decoder_1 (.out0(decoder_1_out0), .out1(decoder_1_out1), .sel(in_10), .en(in_9));
  Clock clock_1 (.out(clock_1_out));
  Counter counter_1 (
    .load(in_1), .D(in_2), .count(in_3), .Q(counter_1_q), .carry(counter_1_carry), .clk(in_4),
    .clr(counter_1_carry));
  Counter counter_2 (
    .load(in_6), .D(in_7), .count(in_7[0]), .Q(counter_2_q), .carry(counter_2_carry), .clk(clock_1_out),
    .clr(counter_2_carry));
  assign out_11 = in_4 ? counter_1_q : 8'bz;  // Controlled_Buffer controlled_buffer_1
  not not_1 (not_1_out, in_4);
  Bit_Extender #(.out_width(7)) bit_extender_1 (.in(counter_2_q), .out(bit_extender_1_out));
  RAM ram_1 (.data(out_11), .sel(decoder_1_out0), .clk(clock_1_out), .ld(not_1_out));  // open: addr, clr
  ROM #(.addrWidth(7)) rom_1 (.addr(bit_extender_1_out), .data(out_11), .sel(decoder_1_out1));
  Bit_Extender #(.out_width(7)) bit_extender_2 (.in(out_11), .out(bit_extender_2_out));
  TTY tty_1 (.data(bit_extender_2_out), .we(in_5));  // open: clk, clr
  // Pins of 1 and 8 bits meet at in_7

  assign in_8 = in_7[0];
endmodule
