// Logisim project LAB-R2.circ as structural Verilog: 1 circuit, main circuit main
module main (
  input  in_1,
  input  [7:0] in_2,
  input  in_3,
  input  in_4,
  input  in_5,
  output [7:0] out_6
);

  wire clock_1_out, decoder_1_out0, decoder_1_out1, not_1_out;
  wire [7:0] controlled_buffer_1_out, controlled_buffer_2_out, controlled_buffer_3_out, register_1_q,
       register_2_q;

  Decoder decoder_1 (.out0(decoder_1_out0), .out1(decoder_1_out1), .sel(in_3), .en(in_4));
  assign controlled_buffer_1_out = in_1 ? in_2 : 8'bz;  // Controlled_Buffer controlled_buffer_1
  Clock clock_1 (.out(clock_1_out));
  not not_1 (not_1_out, in_1);
  Register register_1 (
    .D(controlled_buffer_1_out), .en(decoder_1_out0), .Q(register_1_q), .clk(clock_1_out), .clr(in_5));
  Register register_2 (
    .D(controlled_buffer_1_out), .en(decoder_1_out1), .Q(register_2_q), .clk(clock_1_out), .clr(in_5));
  assign controlled_buffer_2_out = not_1_out ? register_1_q : 8'bz;  // Controlled_Buffer controlled_buffer_2
  assign controlled_buffer_3_out = not_1_out ? register_2_q : 8'bz;  // Controlled_Buffer controlled_buffer_3
  Multiplexer #(.width(8)) multiplexer_1 (
    .in0(controlled_buffer_2_out), .in1(controlled_buffer_3_out), .out(out_6), .sel(in_3), .en(in_4));
endmodule
