// Logisim project LAB-R3.circ as structural Verilog: 1 circuit, main circuit main
module main (
  input  [7:0] in_1,
  input  in_2,
  input  in_3,
  output [7:0] out_4
);

  wire clock_1_out, decoder_1_out0, decoder_1_out1, undriven;
  wire [7:0] register_1_q, register_2_q;

  Decoder decoder_1 (.out0(decoder_1_out0), .out1(decoder_1_out1), .sel(in_2), .en(in_3));
  Clock clock_1 (.out(clock_1_out));
  Register register_1 (.D(in_1), .en(decoder_1_out0), .Q(register_1_q), .clk(clock_1_out), .clr(undriven));
  Register register_2 (.D(in_1), .en(decoder_1_out1), .Q(register_2_q), .clk(clock_1_out), .clr(undriven));
  Multiplexer #(.width(8)) multiplexer_1 (.in0(register_1_q), .in1(register_2_q), .out(out_4), .sel(in_2), .en(in_3));
endmodule
