// Logisim project LAB-R4.circ as structural Verilog: 1 circuit, main circuit main
module main (
  input  [7:0] in_1,
  input  [2:0] in_2,
  input  [7:0] in_3,
  input  [7:0] in_4,
  input  [7:0] in_5,
  input  [1:0] in_6,
  input  in_7,
  output [7:0] out_8
);

  wire [7:0] shifter_1_out, shifter_2_out, shifter_3_out, shifter_4_out;

  Shifter shifter_1 (.in(in_1), .\dist (in_2), .out(shifter_1_out));
  Shifter #(.shift("rl")) shifter_2 (.in(in_3), .\dist (in_2), .out(shifter_2_out));
  Shifter #(.shift("ar")) shifter_3 (.in(in_4), .\dist (in_2), .out(shifter_3_out));
  Shifter #(.shift("rr")) shifter_4 (.in(in_5), .\dist (in_2), .out(shifter_4_out));
  Multiplexer #(.select(2), .width(8)) multiplexer_1 (
    .in0(shifter_1_out), .in1(shifter_2_out), .in2(shifter_3_out), .in3(shifter_4_out), .out(out_8),
    .sel(in_6), .en(in_7));
endmodule
