// Logisim project LAB1-FS.circ as structural Verilog: 2 circuits, main circuit FA
module FA (
  input  A,
  input  B,
  input  C,
  output SUM,
  output CARRY
);

  wire and_1_out, and_2_out, not_1_out, not_2_out, xor_1_out;

  not not_1 (not_1_out, B);
  and and_1 (and_1_out, A, not_1_out);
  xor xor_1 (xor_1_out, A, B);
  not not_2 (not_2_out, C);
  and and_2 (and_2_out, xor_1_out, not_2_out);
  xor xor_2 (SUM, xor_1_out, C);
  or or_1 (CARRY, and_2_out, and_1_out);
endmodule

module FA_U (
  input  A,
  input  B,
  input  C,
  output SUM,
  output CARRY
);

  wire and_1_out, and_2_out, not_1_out, not_2_out, xor_1_out, xor_2_out;

  xor xor_1 (xor_1_out, A, B);
  xor xor_2 (xor_2_out, A, B);
  not not_1 (not_1_out, C);
  not not_2 (not_2_out, B);
  xor xor_3 (SUM, xor_1_out, C);
  and and_1 (and_1_out, xor_2_out, not_1_out);
  and and_2 (and_2_out, A, not_2_out);
  or or_1 (CARRY, and_1_out, and_2_out);
endmodule
