// Logisim project LAB1-Q1-A.circ as structural Verilog: 1 circuit, main circuit Ckt
module Ckt (
  input  A,
  input  B,
  output C,
  output D,
  output E,
  output F,
  output G
);

  not NOT (C, A);
  and AND (D, A, B);
  or OR (E, A, B);
  nand NAND (F, A, B);
  xor XOR (G, A, B);
endmodule
