// Logisim project LAB1-Q1-B.circ as structural Verilog: 1 circuit, main circuit Ckt
module Ckt (
  input  [3:0] A,
  input  [3:0] B,
  output [3:0] C,
  output [3:0] D,
  output [3:0] E,
  output [3:0] F,
  output [3:0] G
);

  assign C = ~A;  // NOT_Gate NOT, 4 bits wide
  assign D = A & B;  // AND_Gate AND, 4 bits wide
  assign E = A | B;  // OR_Gate OR, 4 bits wide
  assign F = ~(A & B);  // NAND_Gate NAND, 4 bits wide
  assign G = A ^ B;  // XOR_Gate XOR, 4 bits wide
endmodule
