// Logisim project LAB1-Q2-B.circ as structural Verilog: 1 circuit, main circuit Ckt
module Ckt (
  input  [7:0] A,
  input  [7:0] B,
  input  [7:0] X,
  input  [7:0] Y,
  output [7:0] C
);

  wire [7:0] nand_1_out, nand_2_out, nand_3_out, nand_4_out, nand_5_out, nand_6_out, nand_7_out, nand_8_out,
       nand_9_out, nand_10_out, nand_11_out, nand_12_out, nand_13_out, nand_14_out, nand_15_out, nand_16_out,
       nand_17_out, nand_18_out, nand_19_out, nand_20_out, nand_21_out;

  assign nand_1_out = ~(A & A);  // NAND_Gate nand_1, 8 bits wide
  assign nand_2_out = ~(B & B);  // NAND_Gate nand_2, 8 bits wide
  assign nand_3_out = ~(A & A);  // NAND_Gate nand_3, 8 bits wide
  assign nand_4_out = ~(B & B);  // NAND_Gate nand_4, 8 bits wide
  assign nand_5_out = ~(nand_1_out & nand_2_out);  // NAND_Gate nand_5, 8 bits wide
  assign nand_6_out = ~(nand_3_out & B);  // NAND_Gate nand_6, 8 bits wide
  assign nand_7_out = ~(A & nand_4_out);  // NAND_Gate nand_7, 8 bits wide
  assign nand_8_out = ~(A & B);  // NAND_Gate nand_8, 8 bits wide
  assign nand_9_out = ~(nand_5_out & nand_5_out);  // NAND_Gate nand_9, 8 bits wide
  assign nand_10_out = ~(nand_6_out & nand_6_out);  // NAND_Gate nand_10, 8 bits wide
  assign nand_11_out = ~(nand_7_out & nand_7_out);  // NAND_Gate nand_11, 8 bits wide
  assign nand_12_out = ~(nand_8_out & nand_8_out);  // NAND_Gate nand_12, 8 bits wide
  assign nand_13_out = ~(Y & Y);  // NAND_Gate nand_13, 8 bits wide
  assign nand_14_out = ~(nand_9_out & Y);  // NAND_Gate nand_14, 8 bits wide
  assign nand_15_out = ~(nand_10_out & X);  // NAND_Gate nand_15, 8 bits wide
  assign nand_16_out = ~(nand_11_out & X);  // NAND_Gate nand_16, 8 bits wide
  assign nand_17_out = ~(nand_12_out & nand_13_out);  // NAND_Gate nand_17, 8 bits wide
  assign nand_18_out = ~(nand_14_out & nand_15_out);  // NAND_Gate nand_18, 8 bits wide
  assign nand_19_out = ~(nand_16_out & nand_17_out);  // NAND_Gate nand_19, 8 bits wide
  assign nand_20_out = ~(nand_18_out & nand_18_out);  // NAND_Gate nand_20, 8 bits wide
  assign nand_21_out = ~(nand_19_out & nand_19_out);  // NAND_Gate nand_21, 8 bits wide
  assign C = ~(nand_20_out & nand_21_out);  // NAND_Gate nand_22, 8 bits wide
endmodule
