// Logisim project LAB1-Q3.circ as structural Verilog: 1 circuit, main circuit Ckt
module Ckt (
  input  A,
  input  B,
  input  C,
  output D
);

  wire nand_1_out, nand_2_out, nand_3_out, nand_4_out, nand_5_out;

  nand nand_1 (nand_1_out, B, C);
  nand nand_2 (nand_2_out, A, C);
  nand nand_3 (nand_3_out, nand_1_out, nand_2_out);
  nand nand_4 (nand_4_out, nand_3_out, nand_3_out);
  nand nand_5 (nand_5_out, A, B);
  nand nand_6 (D, nand_4_out, nand_5_out);
endmodule
