// Logisim project LAB1-Q4.circ as structural Verilog: 1 circuit, main circuit main
module main (
  input  A,
  input  B,
  input  C
);

  wire and_1_out, and_2_out, and_3_out, and_4_out, and_5_out, and_6_out, and_7_out, and_8_out, and_9_out,
       and_10_out, and_11_out, not_1_out, not_2_out, not_3_out, not_4_out, not_6_out, not_7_out, or_1_out,
       or_3_out, or_5_out;
  wire [2:0] not_5_out;

  Hex_Digit_Display hex_digit_display_1 (.value({1'b0, A, B, C}), .dp(1'b0));
  and and_1 (and_1_out, B, C);
  and and_2 (and_2_out, A, C);
  not not_1 (not_1_out, A);
  not not_2 (not_2_out, B);
  not not_3 (not_3_out, A);
  not not_4 (not_4_out, B);
  not not_5 (not_5_out[0], C);
  or or_1 (or_1_out, and_1_out, and_2_out);
  and and_3 (and_3_out, A, B);
  and and_4 (and_4_out, not_1_out, not_2_out);
  and and_5 (and_5_out, not_3_out, B);
  not not_6 (not_6_out, C);
  and and_6 (and_6_out, A, not_4_out);
  not not_7 (not_7_out, C);
  and and_7 (and_7_out, A, B);
  or or_2 (not_5_out[2], or_1_out, and_3_out);
  and and_8 (and_8_out, and_4_out, C);
  and and_9 (and_9_out, and_5_out, not_6_out);
  and and_10 (and_10_out, and_6_out, not_7_out);
  and and_11 (and_11_out, and_7_out, C);
  or or_3 (or_3_out, and_8_out, and_9_out);
  or or_4 (not_5_out[1], or_3_out, or_5_out);
  or or_5 (or_5_out, and_10_out, and_11_out);
  Hex_Digit_Display hex_digit_display_2 (.value({1'b0, not_5_out}), .dp(1'b0));
endmodule
