// Logisim project LAB2-FA.circ as structural Verilog: 2 circuits, main circuit HA
module FA (
  input  in_1,
  input  in_2,
  input  in_3,
  output out_4,
  output out_5
);

  wire ha_1_carry, ha_1_sum, ha_2_carry;

  HA ha_1 (.A(in_2), .B(in_3), .Sum(ha_1_sum), .Carry(ha_1_carry));
  HA ha_2 (.A(in_1), .B(ha_1_sum), .Sum(out_4), .Carry(ha_2_carry));
  or or_1 (out_5, ha_2_carry, ha_1_carry);
endmodule

module HA (
  input  A,
  input  B,
  output Sum,
  output Carry
);

  xor xor_1 (Sum, A, B);
  and and_1 (Carry, A, B);
endmodule
