// Logisim project LAB2-FS.circ as structural Verilog: 4 circuits, main circuit HS
// FS
module FS_2 (
  input  A,
  input  B,
  input  C,
  output Difference,
  output Borrow
);

  wire hs_1_borrow, hs_1_difference, hs_2_borrow;

  HS hs_1 (.A(B), .B(C), .Difference(hs_1_difference), .Borrow(hs_1_borrow));
  HS hs_2 (.A(A), .B(hs_1_difference), .Difference(Difference), .Borrow(hs_2_borrow));
  or or_1 (Borrow, hs_2_borrow, hs_1_borrow);
endmodule

// FS
module FS_1 (
  input  A,
  input  B,
  input  C,
  output Defference,
  output Borrow
);

  wire hs_1_borrow, hs_1_difference, hs_2_borrow;

  HS hs_1 (.A(B), .B(C), .Difference(hs_1_difference), .Borrow(hs_1_borrow));
  HS hs_2 (.A(A), .B(hs_1_difference), .Difference(Defference), .Borrow(hs_2_borrow));
  OR or_1 (.A(hs_2_borrow), .B(hs_1_borrow), .D(Borrow));
endmodule

module HS (
  input  A,
  input  B,
  output Difference,
  output Borrow
);

  wire not_1_out;

  not not_1 (not_1_out, A);
  xor xor_1 (Difference, A, B);
  and and_1 (Borrow, B, not_1_out);
endmodule

module OR (
  input  A,
  input  B,
  output D
);

  or OR (D, A, B);
endmodule
