// Logisim project LAB2-Q1-HA.circ as structural Verilog: 1 circuit, main circuit HA
module HA (
  input  A,
  input  B,
  output Sum,
  output Carry
);

  xor xor_1 (Sum, A, B);
  and and_1 (Carry, A, B);
endmodule
