// Logisim project LAB2-Q2-FA.circ as structural Verilog: 1 circuit, main circuit FA
module FA (
  input  A,
  input  B,
  input  C,
  output Defference,
  output Borrow
);

  wire AND_2_out, AND_out, XOR_out;

  xor XOR (XOR_out, A, B);
  xor XOR_2 (Defference, XOR_out, C);
  and AND (AND_out, C, XOR_out);
  and AND_2 (AND_2_out, A, A);
  or OR (Borrow, AND_out, AND_2_out);
endmodule
