// Logisim project LAB2-Q2-FS.circ as structural Verilog: 1 circuit, main circuit FS
module FS (
  input  A,
  input  B,
  input  C,
  output Defference,
  output Borrow
);

  wire AND_2_out, AND_out, NOT_2_out, NOT_out, XOR_out;

  not NOT (NOT_out, B);
  xor XOR (XOR_out, A, B);
  and AND (AND_out, A, NOT_out);
  not NOT_2 (NOT_2_out, C);
  xor XOR_2 (Defference, XOR_out, C);
  and AND_2 (AND_2_out, XOR_out, NOT_2_out);
  or OR (Borrow, AND_2_out, AND_out);
endmodule
