// Logisim project LAB2-Q3,4.circ as structural Verilog: 5 circuits, main circuit HA
// FAS
module FAS_Q4 (
  input  C0,
  input  B3,
  input  A3,
  input  B2,
  input  A2,
  input  B1,
  input  A1,
  input  B0,
  input  A0
);

  wire fa_2_carry, fa_3_carry, fa_4_carry, or_1_out, or_2_out, or_3_out, or_4_out;
  wire [3:0] fa_4_sum;
  wire [3:3] fa_1_carry;

  Hex_Digit_Display hex_digit_display_1 (.value({fa_1_carry[3], 3'b000}));  // open: dp
  or or_1 (or_1_out, B3, C0);
  or or_2 (or_2_out, B2, C0);
  FA fa_1 (.A(A3), .B(fa_2_carry), .C(or_1_out), .Sum(fa_4_sum[3]), .Carry(fa_1_carry[3]));
  FA fa_2 (.A(A2), .B(fa_3_carry), .C(or_2_out), .Sum(fa_4_sum[2]), .Carry(fa_2_carry));
  or or_3 (or_3_out, B1, C0);
  FA fa_3 (.A(A1), .B(fa_4_carry), .C(or_3_out), .Sum(fa_4_sum[1]), .Carry(fa_3_carry));
  or or_4 (or_4_out, B0, C0);
  FA fa_4 (.A(A0), .B(C0), .C(or_4_out), .Sum(fa_4_sum[0]), .Carry(fa_4_carry));
  Hex_Digit_Display hex_digit_display_2 (.value(fa_4_sum));  // open: dp
endmodule

// RCA
module RCA_Q3 (
  input  B3,
  input  A3,
  input  B2,
  input  A2,
  input  B1,
  input  A1,
  input  B0,
  input  A0
);

  wire fa_1_sum, fa_2_carry, fa_3_carry, ha_1_carry;
  wire [3:0] ha_1_sum;
  wire [3:3] fa_1_carry;

  Hex_Digit_Display hex_digit_display_1 (.value({fa_1_carry[3], 3'b000}));  // open: dp
  FA fa_1 (.A(A3), .B(fa_2_carry), .C(B3), .Sum(fa_1_sum), .Carry(fa_1_carry[3]));
  FA fa_2 (.A(A2), .B(fa_3_carry), .C(B2), .Sum(ha_1_sum[2]), .Carry(fa_2_carry));
  FA fa_3 (.A(A1), .B(ha_1_carry), .C(B1), .Sum(ha_1_sum[1]), .Carry(fa_3_carry));
  HA ha_1 (.A(A0), .B(B0), .Sum(ha_1_sum[0]), .Carry(ha_1_carry));
  Hex_Digit_Display hex_digit_display_2 (.value(ha_1_sum));  // open: dp
endmodule

module FA (
  input  A,
  input  B,
  input  C,
  output Sum,
  output Carry
);

  wire ha_1_carry, ha_1_sum, ha_2_carry;

  HA ha_1 (.A(B), .B(C), .Sum(ha_1_sum), .Carry(ha_1_carry));
  HA ha_2 (.A(A), .B(ha_1_sum), .Sum(Sum), .Carry(ha_2_carry));
  OR or_1 (.A(ha_2_carry), .B(ha_1_carry), .C(Carry));
endmodule

module HA (
  input  A,
  input  B,
  output Sum,
  output Carry
);

  xor xor_1 (Sum, A, B);
  and and_1 (Carry, A, B);
endmodule

module OR (
  input  A,
  input  B,
  output C
);

  or OR (C, A, B);
endmodule
