// Logisim project LAB3-( Decoder, Encoder).circ as structural Verilog: 6 circuits, main circuit Decoder
module Decoder_3 (
  input  A0,
  input  A1,
  input  A2,
  output I0,
  output I1,
  output I2,
  output I3,
  output I4,
  output I5,
  output I6,
  output I7
);

  wire nand_1_out, nand_2_out, nand_3_out, nand_4_out, nand_5_out, nand_6_out, nand_7_out, nand_8_out,
       nand_9_out, nand_10_out, nand_11_out, nand_12_out, nand_13_out, nand_14_out, nand_15_out, nand_16_out,
       nand_17_out, nand_18_out, nand_19_out, nand_20_out, nand_21_out, nand_22_out, nand_23_out,
       nand_24_out, nand_25_out, nand_26_out, nand_27_out, nand_28_out, nand_29_out, nand_30_out,
       nand_33_out, nand_34_out, nand_35_out, nand_36_out, nand_37_out, nand_38_out;

  nand nand_1 (nand_1_out, A0, A1);
  nand nand_2 (nand_2_out, A0, A1);
  nand nand_3 (nand_3_out, A1, A1);
  nand nand_4 (nand_4_out, A1, A1);
  nand nand_5 (nand_5_out, A0, A0);
  nand nand_6 (nand_6_out, A0, A0);
  nand nand_7 (nand_7_out, A0, A0);
  nand nand_8 (nand_8_out, A1, A1);
  nand nand_9 (nand_9_out, A0, A0);
  nand nand_10 (nand_10_out, A1, A1);
  nand nand_11 (nand_11_out, nand_1_out, nand_1_out);
  nand nand_12 (nand_12_out, nand_2_out, nand_2_out);
  nand nand_13 (nand_13_out, A2, A2);
  nand nand_14 (nand_14_out, A0, nand_3_out);
  nand nand_15 (nand_15_out, A0, nand_4_out);
  nand nand_16 (nand_16_out, nand_5_out, A1);
  nand nand_17 (nand_17_out, nand_6_out, A1);
  nand nand_18 (nand_18_out, nand_7_out, nand_8_out);
  nand nand_19 (nand_19_out, nand_9_out, nand_10_out);
  nand nand_20 (nand_20_out, nand_11_out, A2);
  nand nand_21 (nand_21_out, nand_12_out, nand_13_out);
  nand nand_22 (nand_22_out, nand_14_out, nand_14_out);
  nand nand_23 (nand_23_out, nand_15_out, nand_15_out);
  nand nand_24 (nand_24_out, A2, A2);
  nand nand_25 (nand_25_out, nand_16_out, nand_16_out);
  nand nand_26 (nand_26_out, nand_17_out, nand_17_out);
  nand nand_27 (nand_27_out, A2, A2);
  nand nand_28 (nand_28_out, nand_18_out, nand_18_out);
  nand nand_29 (nand_29_out, nand_19_out, nand_19_out);
  nand nand_30 (nand_30_out, A2, A2);
  nand nand_31 (I0, nand_20_out, nand_20_out);
  nand nand_32 (I1, nand_21_out, nand_21_out);
  nand nand_33 (nand_33_out, nand_22_out, A2);
  nand nand_34 (nand_34_out, nand_23_out, nand_24_out);
  nand nand_35 (nand_35_out, nand_25_out, A2);
  nand nand_36 (nand_36_out, nand_26_out, nand_27_out);
  nand nand_37 (nand_37_out, nand_28_out, A2);
  nand nand_38 (nand_38_out, nand_29_out, nand_30_out);
  nand nand_39 (I2, nand_33_out, nand_33_out);
  nand nand_40 (I3, nand_34_out, nand_34_out);
  nand nand_41 (I4, nand_35_out, nand_35_out);
  nand nand_42 (I5, nand_36_out, nand_36_out);
  nand nand_43 (I6, nand_37_out, nand_37_out);
  nand nand_44 (I7, nand_38_out, nand_38_out);
endmodule

module Decoder_2 (
  input  A0,
  input  A1,
  input  A2,
  output I0,
  output I1,
  output I2,
  output I3,
  output I4,
  output I5,
  output I6,
  output I7
);

  wire and_1_out, and_2_out, and_5_out, and_6_out, and_7_out, and_8_out, and_9_out, and_10_out, not_1_out,
       not_2_out, not_3_out, not_4_out, not_5_out, not_6_out, not_7_out, not_8_out, not_9_out, not_10_out,
       not_11_out, not_12_out;

  and and_1 (and_1_out, A0, A1);
  and and_2 (and_2_out, A0, A1);
  not not_1 (not_1_out, A2);
  not not_2 (not_2_out, A1);
  not not_3 (not_3_out, A1);
  not not_4 (not_4_out, A0);
  not not_5 (not_5_out, A0);
  not not_6 (not_6_out, A0);
  not not_7 (not_7_out, A1);
  not not_8 (not_8_out, A0);
  not not_9 (not_9_out, A1);
  and and_3 (I0, and_1_out, A2);
  and and_4 (I1, and_2_out, not_1_out);
  and and_5 (and_5_out, A0, not_2_out);
  and and_6 (and_6_out, A0, not_3_out);
  not not_10 (not_10_out, A2);
  and and_7 (and_7_out, not_4_out, A1);
  and and_8 (and_8_out, not_5_out, A1);
  not not_11 (not_11_out, A2);
  and and_9 (and_9_out, not_6_out, not_7_out);
  and and_10 (and_10_out, not_8_out, not_9_out);
  not not_12 (not_12_out, A2);
  and and_11 (I2, and_5_out, A2);
  and and_12 (I3, and_6_out, not_10_out);
  and and_13 (I4, and_7_out, A2);
  and and_14 (I5, and_8_out, not_11_out);
  and and_15 (I6, and_9_out, A2);
  and and_16 (I7, and_10_out, not_12_out);
endmodule

module Decoder (
  input  A0,
  input  A1,
  input  A2,
  output I0,
  output I1,
  output I2,
  output I3,
  output I4,
  output I5,
  output I6,
  output I7
);

  wire nand_1_out, nand_2_out, nand_3_out, nand_4_out, nand_5_out, nand_6_out, nand_7_out, nand_8_out,
       nand_9_out, nand_10_out, nand_11_out, nand_12_out, nand_13_out, nand_15_out, nand_16_out, nand_17_out,
       nand_18_out, nand_19_out, nand_20_out, nand_21_out;

  nand nand_1 (nand_1_out, A0, A1, A2);
  nand nand_2 (nand_2_out, A2, A2);
  nand nand_3 (nand_3_out, A1, A1);
  nand nand_4 (nand_4_out, A1, A1);
  nand nand_5 (nand_5_out, A2, A2);
  nand nand_6 (nand_6_out, A0, A0);
  nand nand_7 (nand_7_out, A0, A0);
  nand nand_8 (nand_8_out, A2, A2);
  nand nand_9 (nand_9_out, A0, A0);
  nand nand_10 (nand_10_out, A1, A1);
  nand nand_11 (nand_11_out, A0, A0);
  nand nand_12 (nand_12_out, A1, A1);
  nand nand_13 (nand_13_out, A2, A2);
  nand nand_14 (I0, nand_1_out, nand_1_out);
  nand nand_15 (nand_15_out, A0, A1, nand_2_out);
  nand nand_16 (nand_16_out, A0, nand_3_out, A2);
  nand nand_17 (nand_17_out, A0, nand_4_out, nand_5_out);
  nand nand_18 (nand_18_out, nand_6_out, A1, A2);
  nand nand_19 (nand_19_out, nand_7_out, A1, nand_8_out);
  nand nand_20 (nand_20_out, nand_9_out, nand_10_out, A2);
  nand nand_21 (nand_21_out, nand_11_out, nand_12_out, nand_13_out);
  nand nand_22 (I1, nand_15_out, nand_15_out);
  nand nand_23 (I2, nand_16_out, nand_16_out);
  nand nand_24 (I3, nand_17_out, nand_17_out);
  nand nand_25 (I4, nand_18_out, nand_18_out);
  nand nand_26 (I5, nand_19_out, nand_19_out);
  nand nand_27 (I6, nand_20_out, nand_20_out);
  nand nand_28 (I7, nand_21_out, nand_21_out);
endmodule

module Encoder_3 (
  input  I0,
  input  I1,
  input  I2,
  input  I3,
  input  I4,
  input  I5,
  input  I6,
  input  I7,
  output A0,
  output A1,
  output A2
);

  wire nand_1_out, nand_2_out, nand_3_out, nand_4_out, nand_5_out, nand_6_out, nand_7_out, nand_8_out,
       nand_9_out, nand_10_out, nand_11_out, nand_12_out, nand_13_out, nand_14_out, nand_15_out, nand_16_out,
       nand_17_out, nand_18_out, nand_19_out, nand_20_out, nand_21_out, nand_22_out, nand_23_out, nand_24_out;

  nand nand_1 (nand_1_out, I1, I1);
  nand nand_2 (nand_2_out, I3, I3);
  nand nand_3 (nand_3_out, I5, I5);
  nand nand_4 (nand_4_out, I7, I7);
  nand nand_5 (nand_5_out, I2, I2);
  nand nand_6 (nand_6_out, I3, I3);
  nand nand_7 (nand_7_out, I6, I6);
  nand nand_8 (nand_8_out, I7, I7);
  nand nand_9 (nand_9_out, I4, I4);
  nand nand_10 (nand_10_out, I5, I5);
  nand nand_11 (nand_11_out, I6, I6);
  nand nand_12 (nand_12_out, I7, I7);
  nand nand_13 (nand_13_out, nand_1_out, nand_2_out);
  nand nand_14 (nand_14_out, nand_3_out, nand_4_out);
  nand nand_15 (nand_15_out, nand_5_out, nand_6_out);
  nand nand_16 (nand_16_out, nand_7_out, nand_8_out);
  nand nand_17 (nand_17_out, nand_9_out, nand_10_out);
  nand nand_18 (nand_18_out, nand_11_out, nand_12_out);
  nand nand_19 (nand_19_out, nand_13_out, nand_13_out);
  nand nand_20 (nand_20_out, nand_14_out, nand_14_out);
  nand nand_21 (nand_21_out, nand_15_out, nand_15_out);
  nand nand_22 (nand_22_out, nand_16_out, nand_16_out);
  nand nand_23 (nand_23_out, nand_17_out, nand_17_out);
  nand nand_24 (nand_24_out, nand_18_out, nand_18_out);
  nand nand_25 (A0, nand_19_out, nand_20_out);
  nand nand_26 (A1, nand_21_out, nand_22_out);
  nand nand_27 (A2, nand_23_out, nand_24_out);
endmodule

module Encoder_2 (
  input  I0,
  input  I1,
  input  I2,
  input  I3,
  input  I4,
  input  I5,
  input  I6,
  input  I7,
  output A0,
  output A1,
  output A2
);

  wire or_1_out, or_2_out, or_3_out, or_4_out, or_5_out, or_6_out;

  or or_1 (or_1_out, I1, I3);
  or or_2 (or_2_out, I5, I7);
  or or_3 (or_3_out, I2, I3);
  or or_4 (or_4_out, I6, I7);
  or or_5 (or_5_out, I4, I5);
  or or_6 (or_6_out, I6, I7);
  or or_7 (A0, or_1_out, or_2_out);
  or or_8 (A1, or_3_out, or_4_out);
  or or_9 (A2, or_5_out, or_6_out);
endmodule

module Encoder (
  input  I0,
  input  I1,
  input  I2,
  input  I3,
  input  I4,
  input  I5,
  input  I6,
  input  I7,
  output A0,
  output A1,
  output A2
);

  wire nand_1_out, nand_2_out, nand_3_out, nand_4_out, nand_5_out, nand_6_out, nand_7_out, nand_8_out,
       nand_9_out, nand_10_out, nand_11_out, nand_12_out;

  nand nand_1 (nand_1_out, I1, I1);
  nand nand_2 (nand_2_out, I3, I3);
  nand nand_3 (nand_3_out, I5, I5);
  nand nand_4 (nand_4_out, I7, I7);
  nand nand_5 (nand_5_out, I2, I2);
  nand nand_6 (nand_6_out, I3, I3);
  nand nand_7 (nand_7_out, I6, I6);
  nand nand_8 (nand_8_out, I7, I7);
  nand nand_9 (nand_9_out, I4, I4);
  nand nand_10 (nand_10_out, I5, I5);
  nand nand_11 (nand_11_out, I6, I6);
  nand nand_12 (nand_12_out, I7, I7);
  nand nand_13 (A0, nand_1_out, nand_2_out, nand_3_out, nand_4_out);
  nand nand_14 (A1, nand_5_out, nand_6_out, nand_7_out, nand_8_out);
  nand nand_15 (A2, nand_9_out, nand_10_out, nand_11_out, nand_12_out);
endmodule
