// Logisim project LAB3-MUX-1.circ as structural Verilog: 4 circuits, main circuit 2X1 MUX
// 16X1
module _16X1_MUX (
  input  I0,
  input  I1,
  input  I3,
  input  I4,
  input  I5,
  input  I6,
  input  I7,
  input  I8,
  input  S0,
  input  S1,
  input  S2,
  input  S3,
  input  I9,
  input  I10,
  input  I11,
  input  I12,
  input  I13,
  input  I14,
  input  I15,
  input  I16,
  output O
);

  wire n8x1_mux_1_o, n8x1_mux_2_o;

  _8X1_MUX u_8x1_mux_1 (
    .I0(I0), .I1(I1), .I2(I3), .I3(I4), .I4(I5), .S0(I6), .I5(I7), .I6(I8), .I7(S0), .S1(S1), .S2(S2),
    .O(n8x1_mux_1_o));
  _8X1_MUX u_8x1_mux_2 (
    .I0(I9), .I1(I10), .I2(I11), .I3(I12), .I4(I13), .S0(I14), .I5(I15), .I6(I16), .I7(S0), .S1(S2), .S2(S2),
    .O(n8x1_mux_2_o));
  _2X1_MUX u_2x1_mux_1 (.I0(n8x1_mux_1_o), .I1(n8x1_mux_2_o), .S(S3), .O(O));
endmodule

// 8X1
module _8X1_MUX (
  input  I0,
  input  I1,
  input  I2,
  input  I3,
  input  I4,
  input  S2,
  input  S0,
  input  I5,
  input  I6,
  input  I7,
  input  S1,
  output O
);

  wire n4x1_mux_1_o, n4x1_mux_2_o;

  _4X1_MUX u_4x1_mux_1 (.I0(I0), .I1(I1), .I2(I2), .S0(I3), .I3(S0), .S1(S1), .O(n4x1_mux_1_o));
  _4X1_MUX u_4x1_mux_2 (.I0(I4), .I1(I5), .I2(I6), .S0(I7), .I3(S0), .S1(S1), .O(n4x1_mux_2_o));
  _2X1_MUX u_2x1_mux_1 (.I0(n4x1_mux_1_o), .I1(n4x1_mux_2_o), .S(S2), .O(O));
endmodule

// 4X1
module _4X1_MUX (
  input  I0,
  input  I1,
  input  I2,
  input  S0,
  input  S1,
  input  I3,
  output O
);

  wire n2x1_mux_1_o, n2x1_mux_2_o;

  _2X1_MUX u_2x1_mux_1 (.I0(I0), .I1(I1), .S(S0), .O(n2x1_mux_1_o));
  _2X1_MUX u_2x1_mux_2 (.I0(I2), .I1(I3), .S(S0), .O(n2x1_mux_2_o));
  _2X1_MUX u_2x1_mux_3 (.I0(n2x1_mux_1_o), .I1(n2x1_mux_2_o), .S(S1), .O(O));
endmodule

// 2X1
module _2X1_MUX (
  input  I0,
  input  I1,
  input  S,
  output O
);

  wire and_1_out, and_2_out, not_1_out;

  not not_1 (not_1_out, S);
  and and_1 (and_1_out, I0, not_1_out);
  and and_2 (and_2_out, I1, S);
  or or_1 (O, and_1_out, and_2_out);
endmodule
