// Logisim project LAB3-MUX.circ as structural Verilog
// GATES
module MUX (
  input  A,
  input  B,
  input  C,
  input  D,
  input  E,
  input  F,
  output Y
);

  wire and_1_out, and_2_out, and_3_out, and_4_out, not_1_out, not_2_out, not_3_out, not_4_out;

  not not_1 (not_1_out, E);
  not not_2 (not_2_out, F);
  not not_3 (not_3_out, E);
  not not_4 (not_4_out, F);
  and and_1 (and_1_out, not_1_out, not_2_out, A);
  and and_2 (and_2_out, not_3_out, F, B);
  and and_3 (and_3_out, E, not_4_out, C);
  and and_4 (and_4_out, E, F, D);
  or or_1 (Y, and_1_out, and_2_out, and_3_out, and_4_out);
endmodule

// MUX
module NAND (
  input  A,
  input  B,
  input  C,
  input  D,
  input  E,
  input  F,
  output Y
);

  wire nand_1_out, nand_2_out, nand_3_out, nand_4_out, nand_5_out, nand_6_out, nand_7_out, nand_8_out;

  nand nand_1 (nand_1_out, E, E);
  nand nand_2 (nand_2_out, F, F);
  nand nand_3 (nand_3_out, E, E);
  nand nand_4 (nand_4_out, F, F);
  nand nand_5 (nand_5_out, nand_1_out, nand_2_out, A);
  nand nand_6 (nand_6_out, nand_3_out, F, B);
  nand nand_7 (nand_7_out, E, nand_4_out, C);
  nand nand_8 (nand_8_out, E, F, D);
  nand nand_9 (Y, nand_5_out, nand_6_out, nand_7_out, nand_8_out);
endmodule
