// Logisim project LAB3-Q1,2.circ as structural Verilog: 5 circuits, main circuit 2X1 MUX
// 1X8
module _1X8_DMUX_Q2 (
  input  in_1,
  input  in_2,
  input  in_3,
  output out_4,
  output out_5,
  output out_6,
  output out_7,
  output out_8,
  output out_9,
  output out_10,
  output out_11
);

  _4X1_MUX u_4x1_mux_1 (.I0(out_7), .I1(out_6), .I2(out_5), .S0(in_2), .I3(out_4), .O(in_3), .S1(in_1));
  _4X1_MUX u_4x1_mux_2 (.I0(out_11), .I1(out_10), .I2(out_9), .S0(in_2), .I3(out_8), .O(in_3), .S1(in_1));
endmodule

module _16X1_MUX (
  input  in_1,
  input  in_2,
  input  in_3,
  input  in_4,
  input  in_5,
  input  in_6,
  input  in_7,
  input  in_8,
  input  in_9,
  input  in_10,
  input  in_11,
  input  in_12,
  input  in_13,
  input  in_14,
  input  in_15,
  input  in_16,
  input  in_17,
  input  in_18,
  input  in_19,
  input  in_20,
  output out_21
);

  wire n8x1_mux_q1_1_o, n8x1_mux_q1_2_o;

  _8X1_MUX_Q1 u_8x1_mux_q1_1 (
    .I0(in_1), .I1(in_2), .I2(in_3), .I3(in_4), .I4(in_5), .S0(in_18), .I5(in_6), .I6(in_7), .I7(in_8),
    .O(n8x1_mux_q1_1_o), .S1(in_19), .S2(in_20));
  _8X1_MUX_Q1 u_8x1_mux_q1_2 (
    .I0(in_9), .I1(in_11), .I2(in_12), .I3(in_13), .I4(in_14), .S0(in_18), .I5(in_15), .I6(in_16),
    .I7(in_17), .O(n8x1_mux_q1_2_o), .S1(in_19), .S2(in_20));
  _2X1_MUX u_2x1_mux_1 (.I0(n8x1_mux_q1_1_o), .I1(n8x1_mux_q1_2_o), .S(in_10), .O(out_21));
endmodule

// 8X1
module _8X1_MUX_Q1 (
  input  I0,
  input  I1,
  input  I2,
  input  I3,
  input  I4,
  input  S2,
  input  S0,
  input  I5,
  input  I6,
  input  I7,
  input  S1,
  output O
);

  wire n4x1_mux_1_o, n4x1_mux_2_o;

  _4X1_MUX u_4x1_mux_1 (.I0(I0), .I1(I1), .I2(I2), .S0(S0), .I3(I3), .O(n4x1_mux_1_o), .S1(S1));
  _4X1_MUX u_4x1_mux_2 (.I0(I4), .I1(I5), .I2(I6), .S0(S0), .I3(I7), .O(n4x1_mux_2_o), .S1(S1));
  _2X1_MUX u_2x1_mux_1 (.I0(n4x1_mux_1_o), .I1(n4x1_mux_2_o), .S(S2), .O(O));
endmodule

// 4X1
module _4X1_MUX (
  input  I0,
  input  I1,
  input  I2,
  input  S0,
  input  S1,
  input  I3,
  output O
);

  wire n2x1_mux_1_o, n2x1_mux_2_o;

  _2X1_MUX u_2x1_mux_1 (.I0(I0), .I1(I1), .S(S0), .O(n2x1_mux_1_o));
  _2X1_MUX u_2x1_mux_2 (.I0(I2), .I1(I3), .S(S0), .O(n2x1_mux_2_o));
  _2X1_MUX u_2x1_mux_3 (.I0(n2x1_mux_1_o), .I1(n2x1_mux_2_o), .S(S1), .O(O));
endmodule

// 2X1
module _2X1_MUX (
  input  I0,
  input  I1,
  input  S,
  output O
);

  wire and_1_out, and_2_out, not_1_out;

  not not_1 (not_1_out, S);
  and and_1 (and_1_out, I0, not_1_out);
  and and_2 (and_2_out, I1, S);
  or or_1 (O, and_1_out, and_2_out);
endmodule
