// Logisim project LAB3-Q2.circ as structural Verilog: 1 circuit, main circuit main
module main (
  input  S0,
  input  S1,
  input  S2,
  input  in_4,
  output out_5,
  output out_6,
  output out_7,
  output out_8,
  output out_9,
  output out_10,
  output out_11,
  output out_12
);

  wire not_1_out, not_2_out, not_3_out;

  not not_1 (not_1_out, S0);
  not not_2 (not_2_out, S1);
  not not_3 (not_3_out, S2);
  and and_1 (out_5, not_3_out, not_2_out, not_1_out, in_4);
  and and_2 (out_6, S2, not_2_out, not_1_out, in_4);
  and and_3 (out_7, not_3_out, S1, not_1_out, in_4);
  and and_4 (out_8, S2, S1, not_1_out, in_4);
  and and_5 (out_9, not_3_out, not_2_out, S0, in_4);
  and and_6 (out_10, S2, not_2_out, S0, in_4);
  and and_7 (out_11, not_3_out, S1, S0, in_4);
  and and_8 (out_12, S2, S1, S0, in_4);
endmodule
