// Logisim project LAB4-Q1.circ as structural Verilog: 2 circuits, main circuit 4X1 MUX
// 4X1
module _4X1_MUX (
  input  in_1,
  input  in_2,
  input  in_3,
  input  in_4,
  input  [1:0] in_5,
  output out_6
);

  Multiplexer #(.select(2), .enable("false")) multiplexer_1 (
    .in0(in_1), .in1(in_2), .in2(in_3), .in3(in_4), .out(out_6), .sel(in_5));
endmodule

module _8X1_MUX (
  input  in_1,
  input  in_2,
  input  in_3,
  input  in_4,
  input  in_5,
  input  in_6,
  input  in_7,
  input  in_8,
  input  [2:0] in_9,
  output out_10
);

  Multiplexer #(.select(3), .enable("false")) multiplexer_1 (
    .in0(in_1), .in1(in_2), .in2(in_3), .in3(in_4), .in4(in_5), .in5(in_6), .in6(in_7), .in7(in_8),
    .out(out_10), .sel(in_9));
endmodule
