// Logisim project LAB6-ALU.circ as structural Verilog: 1 circuit, main circuit main
module main (
  input  A1,
  input  B1,
  input  A2,
  input  B2,
  input  A3,
  input  B3,
  input  D0,
  input  D1,
  input  C3,
  input  A3_2,
  input  B3_2,
  output O,
  output O_out
);

  wire adder_1_out, and_1_out, or_1_out, xor_1_out;

  and and_1 (and_1_out, A1, B1);
  or or_1 (or_1_out, A2, B2);
  xor xor_1 (xor_1_out, A3, B3);
  Adder #(.width(1)) adder_1 (.a(A3_2), .b(B3_2), .out(adder_1_out), .cin(C3), .cout(O_out));
  Multiplexer multiplexer_1 (.in0(or_1_out), .in1(adder_1_out), .out(O), .sel(D0), .en(D1));
endmodule
