// Logisim project LAB7-Latch.circ as structural Verilog: 2 circuits, main circuit NAND
module NAND (
  input  S,
  input  R,
  output Q,
  output Q_prime
);

  nand nand_1 (Q, S, Q_prime);
  nand nand_2 (Q_prime, Q, R);
endmodule

module NOR (
  input  S,
  input  R,
  output Q,
  output Q_prime
);

  nor nor_1 (Q, S, Q_prime);
  nor nor_2 (Q_prime, Q, R);
endmodule
