// Logisim project LAB7-Q1.circ as structural Verilog: 2 circuits, main circuit Q1
module Q1 (
  input  PRE,
  input  INP,
  input  E,
  input  CLK,
  input  CLR,
  output Q,
  output Q_prime
);

  wire nand_1_out, nand_2_out, nand_3_out, nand_4_out, nand_5_out, nand_6_out, not_1_out, not_2_out,
       not_3_out, not_4_out;

  not not_1 (not_1_out, INP);
  nand nand_1 (nand_1_out, INP, E, CLK);
  nand nand_2 (nand_2_out, CLK, E, not_1_out);
  not not_2 (not_2_out, PRE);
  not not_3 (not_3_out, CLK);
  not not_4 (not_4_out, CLR);
  nand nand_3 (nand_3_out, nand_1_out, not_2_out, nand_4_out);
  nand nand_4 (nand_4_out, nand_3_out, not_4_out, nand_2_out);
  nand nand_5 (nand_5_out, nand_3_out, not_3_out);
  nand nand_6 (nand_6_out, not_3_out, nand_4_out);
  nand nand_7 (Q, nand_5_out, not_2_out, Q_prime);
  nand nand_8 (Q_prime, Q, not_4_out, nand_6_out);
endmodule

module Q2 (
  input  INP,
  input  PRE,
  input  E,
  input  CLR,
  output Q,
  output Q_prime
);

  wire clock_1_out, q1_1_q, q1_2_q, q1_3_q;

  Clock clock_1 (.out(clock_1_out));
  Q1 q1_1 (.PRE(PRE), .INP(INP), .E(E), .CLR(CLR), .Q(q1_1_q), .CLK(clock_1_out));  // open: Q_prime
  Q1 q1_2 (.PRE(PRE), .INP(q1_1_q), .E(E), .CLR(CLR), .Q(q1_2_q), .CLK(clock_1_out));  // open: Q_prime
  Q1 q1_3 (.PRE(E), .INP(q1_2_q), .E(E), .CLR(CLR), .Q(q1_3_q), .CLK(clock_1_out));  // open: Q_prime
  Q1 q1_4 (.PRE(PRE), .INP(q1_3_q), .E(E), .CLR(CLR), .Q(Q), .Q_prime(Q_prime), .CLK(clock_1_out));
endmodule
