// Logisim project LAB7-Q2.circ as structural Verilog: 1 circuit, main circuit SISO
module SISO (
  input  INP,
  input  PRE,
  input  E,
  input  CLR,
  output out_5
);

  wire clock_1_out, d_ff_1_q, d_ff_2_q, d_ff_3_q;

  Clock clock_1 (.out(clock_1_out));
  D_Flip_Flop d_ff_1 (.clk(clock_1_out), .D(INP), .Q(d_ff_1_q), .preset(PRE), .en(E), .reset(CLR));  // open: Qn
  D_Flip_Flop d_ff_2 (.clk(clock_1_out), .D(d_ff_1_q), .Q(d_ff_2_q), .preset(PRE), .en(E), .reset(CLR));  // open: Qn
  D_Flip_Flop d_ff_3 (.clk(clock_1_out), .D(d_ff_2_q), .Q(d_ff_3_q), .preset(PRE), .en(E), .reset(CLR));  // open: Qn
  D_Flip_Flop d_ff_4 (.clk(clock_1_out), .D(d_ff_3_q), .Q(out_5), .preset(PRE), .en(E), .reset(CLR));  // open: Qn
endmodule
