// Logisim project LAB7-Q3.circ as structural Verilog: 1 circuit, main circuit SIPO
module SIPO (
  input  INP,
  input  CLR,
  input  PRE,
  input  E,
  output out_5,
  output out_6,
  output out_7,
  output out_8
);

  wire clock_1_out;

  Clock clock_1 (.out(clock_1_out));
  D_Flip_Flop d_ff_1 (.clk(clock_1_out), .D(INP), .Q(out_5), .preset(PRE), .en(E), .reset(CLR));  // open: Qn
  D_Flip_Flop d_ff_2 (.clk(clock_1_out), .D(out_5), .Q(out_6), .preset(PRE), .en(E), .reset(CLR));  // open: Qn
  D_Flip_Flop d_ff_3 (.clk(clock_1_out), .D(out_6), .Q(out_7), .preset(PRE), .en(E), .reset(CLR));  // open: Qn
  D_Flip_Flop d_ff_4 (.clk(clock_1_out), .D(out_7), .Q(out_8), .preset(PRE), .en(E), .reset(CLR));  // open: Qn
endmodule
