// Logisim project LAB9-Q1.circ as structural Verilog: 3 circuits, main circuit ROM 8X8 Q1
module ROM_8X8_Q1 (
  input  CLK,
  input  [2:0] Address__Line,
  input  Chip_Select,
  output [7:0] Data_Out
);

  wire demultiplexer_1_out0, demultiplexer_1_out1, demultiplexer_1_out2, demultiplexer_1_out3,
       demultiplexer_1_out4, demultiplexer_1_out5, demultiplexer_1_out6, demultiplexer_1_out7;
  wire [7:0] counter_1_q, counter_2_q, register_1_q, register_2_q, register_3_q, register_4_q, register_5_q,
       register_6_q;

  Demultiplexer #(.select(3)) demultiplexer_1 (
    .out0(demultiplexer_1_out0), .out1(demultiplexer_1_out1), .out2(demultiplexer_1_out2),
    .out3(demultiplexer_1_out3), .out4(demultiplexer_1_out4), .out5(demultiplexer_1_out5),
    .out6(demultiplexer_1_out6), .out7(demultiplexer_1_out7), .sel(Address__Line), .en(Chip_Select));  // open: in
  Register register_1 (.en(demultiplexer_1_out0), .Q(register_1_q), .clk(CLK));  // open: D, clr
  Register register_2 (.en(demultiplexer_1_out1), .Q(register_2_q), .clk(CLK));  // open: D, clr
  Register register_3 (.en(demultiplexer_1_out2), .Q(register_3_q), .clk(CLK));  // open: D, clr
  Counter counter_1 (.count(demultiplexer_1_out3), .Q(counter_1_q), .clk(CLK));  // open: load, D, carry, clr
  Counter counter_2 (.count(demultiplexer_1_out4), .Q(counter_2_q), .clk(CLK));  // open: load, D, carry, clr
  Register register_4 (.en(demultiplexer_1_out5), .Q(register_4_q), .clk(CLK));  // open: D, clr
  Register register_5 (.en(demultiplexer_1_out6), .Q(register_5_q), .clk(CLK));  // open: D, clr
  Register register_6 (.en(demultiplexer_1_out7), .Q(register_6_q), .clk(CLK));  // open: D, clr
  Multiplexer #(.select(3), .width(8)) multiplexer_1 (
    .in0(register_1_q), .in1(register_2_q), .in2(register_3_q), .in3(counter_1_q), .in4(counter_2_q),
    .in5(register_4_q), .in6(register_5_q), .in7(register_6_q), .out(Data_Out), .sel(Address__Line),
    .en(Chip_Select));
endmodule

module RAM_16X8_Q1 (
  input  Write_Read,
  input  [7:0] Data_In,
  input  CLK,
  input  [3:0] Chip_Select,
  input  Address_Line,
  input  CLR,
  output [7:0] Data_Out
);

  wire demultiplexer_1_out0, demultiplexer_1_out1, demultiplexer_1_out2, demultiplexer_1_out3,
       demultiplexer_1_out4, demultiplexer_1_out5, demultiplexer_1_out6, demultiplexer_1_out7,
       demultiplexer_1_out8, demultiplexer_1_out9, demultiplexer_1_out10, demultiplexer_1_out11,
       demultiplexer_1_out12, demultiplexer_1_out13, demultiplexer_1_out14, demultiplexer_1_out15, not_1_out;
  wire [7:0] controlled_buffer_1_out, controlled_buffer_2_out, controlled_buffer_3_out,
       controlled_buffer_4_out, controlled_buffer_5_out, controlled_buffer_6_out, controlled_buffer_7_out,
       controlled_buffer_8_out, controlled_buffer_9_out, controlled_buffer_10_out, controlled_buffer_11_out,
       controlled_buffer_12_out, controlled_buffer_13_out, controlled_buffer_14_out,
       controlled_buffer_15_out, controlled_buffer_16_out, controlled_buffer_17_out, register_1_q,
       register_2_q, register_3_q, register_4_q, register_5_q, register_6_q, register_7_q, register_8_q,
       register_9_q, register_10_q, register_11_q, register_12_q, register_13_q, register_14_q,
       register_15_q, register_16_q;

  Demultiplexer #(.select(4)) demultiplexer_1 (
    .out0(demultiplexer_1_out0), .out1(demultiplexer_1_out1), .out2(demultiplexer_1_out2),
    .out3(demultiplexer_1_out3), .out4(demultiplexer_1_out4), .out5(demultiplexer_1_out5),
    .out6(demultiplexer_1_out6), .out7(demultiplexer_1_out7), .out8(demultiplexer_1_out8),
    .out9(demultiplexer_1_out9), .out10(demultiplexer_1_out10), .out11(demultiplexer_1_out11),
    .out12(demultiplexer_1_out12), .out13(demultiplexer_1_out13), .out14(demultiplexer_1_out14),
    .out15(demultiplexer_1_out15), .sel(Chip_Select), .en(Address_Line));  // open: in
  assign controlled_buffer_1_out = Write_Read ? Data_In : 8'bz;  // Controlled_Buffer controlled_buffer_1
  not not_1 (not_1_out, Write_Read);
  Register register_1 (.D(controlled_buffer_1_out), .en(demultiplexer_1_out0), .Q(register_1_q), .clk(CLK), .clr(CLR));
  Register register_2 (.D(controlled_buffer_1_out), .en(demultiplexer_1_out1), .Q(register_2_q), .clk(CLK), .clr(CLR));
  Register register_3 (.D(controlled_buffer_1_out), .en(demultiplexer_1_out2), .Q(register_3_q), .clk(CLK), .clr(CLR));
  Register register_4 (.D(controlled_buffer_1_out), .en(demultiplexer_1_out3), .Q(register_4_q), .clk(CLK), .clr(CLR));
  Register register_5 (.D(controlled_buffer_1_out), .en(demultiplexer_1_out4), .Q(register_5_q), .clk(CLK), .clr(CLR));
  Register register_6 (.D(controlled_buffer_1_out), .en(demultiplexer_1_out5), .Q(register_6_q), .clk(CLK), .clr(CLR));
  Register register_7 (.D(controlled_buffer_1_out), .en(demultiplexer_1_out6), .Q(register_7_q), .clk(CLK), .clr(CLR));
  Register register_8 (.D(controlled_buffer_1_out), .en(demultiplexer_1_out7), .Q(register_8_q), .clk(CLK), .clr(CLR));
  Register register_9 (.D(controlled_buffer_1_out), .en(demultiplexer_1_out8), .Q(register_9_q), .clk(CLK), .clr(CLR));
  Register register_10 (
    .D(controlled_buffer_1_out), .en(demultiplexer_1_out9), .Q(register_10_q), .clk(CLK), .clr(CLR));
  Register register_11 (
    .D(controlled_buffer_1_out), .en(demultiplexer_1_out10), .Q(register_11_q), .clk(CLK), .clr(CLR));
  Register register_12 (
    .D(controlled_buffer_1_out), .en(demultiplexer_1_out11), .Q(register_12_q), .clk(CLK), .clr(CLR));
  Register register_13 (
    .D(controlled_buffer_1_out), .en(demultiplexer_1_out12), .Q(register_13_q), .clk(CLK), .clr(CLR));
  Register register_14 (
    .D(controlled_buffer_1_out), .en(demultiplexer_1_out13), .Q(register_14_q), .clk(CLK), .clr(CLR));
  Register register_15 (
    .D(controlled_buffer_1_out), .en(demultiplexer_1_out14), .Q(register_15_q), .clk(CLK), .clr(CLR));
  Register register_16 (
    .D(controlled_buffer_1_out), .en(demultiplexer_1_out15), .Q(register_16_q), .clk(CLK), .clr(CLR));
  assign controlled_buffer_2_out = not_1_out ? register_1_q : 8'bz;  // Controlled_Buffer controlled_buffer_2
  assign controlled_buffer_3_out = not_1_out ? register_2_q : 8'bz;  // Controlled_Buffer controlled_buffer_3
  assign controlled_buffer_4_out = not_1_out ? register_3_q : 8'bz;  // Controlled_Buffer controlled_buffer_4
  assign controlled_buffer_5_out = not_1_out ? register_4_q : 8'bz;  // Controlled_Buffer controlled_buffer_5
  assign controlled_buffer_6_out = not_1_out ? register_5_q : 8'bz;  // Controlled_Buffer controlled_buffer_6
  assign controlled_buffer_7_out = not_1_out ? register_6_q : 8'bz;  // Controlled_Buffer controlled_buffer_7
  assign controlled_buffer_8_out = not_1_out ? register_7_q : 8'bz;  // Controlled_Buffer controlled_buffer_8
  assign controlled_buffer_9_out = not_1_out ? register_8_q : 8'bz;  // Controlled_Buffer controlled_buffer_9
  assign controlled_buffer_10_out = not_1_out ? register_9_q : 8'bz;  // Controlled_Buffer controlled_buffer_10
  assign controlled_buffer_11_out = not_1_out ? register_10_q : 8'bz;  // Controlled_Buffer controlled_buffer_11
  assign controlled_buffer_12_out = not_1_out ? register_11_q : 8'bz;  // Controlled_Buffer controlled_buffer_12
  assign controlled_buffer_13_out = not_1_out ? register_12_q : 8'bz;  // Controlled_Buffer controlled_buffer_13
  assign controlled_buffer_14_out = not_1_out ? register_13_q : 8'bz;  // Controlled_Buffer controlled_buffer_14
  assign controlled_buffer_15_out = not_1_out ? register_14_q : 8'bz;  // Controlled_Buffer controlled_buffer_15
  assign controlled_buffer_16_out = not_1_out ? register_15_q : 8'bz;  // Controlled_Buffer controlled_buffer_16
  assign controlled_buffer_17_out = not_1_out ? register_16_q : 8'bz;  // Controlled_Buffer controlled_buffer_17
  Multiplexer #(.select(4), .width(8)) multiplexer_1 (
    .in0(controlled_buffer_2_out), .in1(controlled_buffer_3_out), .in2(controlled_buffer_4_out),
    .in3(controlled_buffer_5_out), .in4(controlled_buffer_6_out), .in5(controlled_buffer_7_out),
    .in6(controlled_buffer_8_out), .in7(controlled_buffer_9_out), .in8(controlled_buffer_10_out),
    .in9(controlled_buffer_11_out), .in10(controlled_buffer_12_out), .in11(controlled_buffer_13_out),
    .in12(controlled_buffer_14_out), .in13(controlled_buffer_15_out), .in14(controlled_buffer_16_out),
    .in15(controlled_buffer_17_out), .out(Data_Out), .sel(Chip_Select), .en(Address_Line));
endmodule

module _56X8_Q2 (
  input  in_1,
  input  in_2,
  input  [1:0] in_3,
  output [7:0] out_4,
  output [7:0] out_5,
  output [7:0] out_6,
  output [7:0] out_7
);

  wire clock_1_out, decoder_1_out0, decoder_1_out1, decoder_1_out2, decoder_1_out3;

  Clock clock_1 (.out(clock_1_out));
  Decoder #(.select(2)) decoder_1 (
    .out0(decoder_1_out0), .out1(decoder_1_out1), .out2(decoder_1_out2), .out3(decoder_1_out3), .sel(in_3),
    .en(in_2));
  // RAM_16X8_Q1 ram_16x8_q1_1: pin names not known; wires that end beside it: clock_1_out, decoder_1_out0, in_1, out_4
  // RAM_16X8_Q1 ram_16x8_q1_2: pin names not known; wires that end beside it: clock_1_out, decoder_1_out1, in_1, out_5
  // RAM_16X8_Q1 ram_16x8_q1_3: pin names not known; wires that end beside it: clock_1_out, decoder_1_out2, in_1, out_6
  ROM_8X8_Q1 rom_8x8_q1_1 (.CLK(clock_1_out), .Chip_Select(decoder_1_out3), .Data_Out(out_7));  // open: Address__Line
endmodule
