// Logisim project LAB9-RAM.circ as structural Verilog: 2 circuits, main circuit RAM 8 Bit
module RAM_8_Bit (
  input  [7:0] in_1,
  input  in_2,
  input  in_3,
  input  in_4,
  output [7:0] out_5
);

  wire clock_1_out;

  Clock clock_1 (.out(clock_1_out));
  RAM ram_1 (.addr(in_1), .data(out_5), .sel(in_2), .clk(clock_1_out), .ld(in_3), .clr(in_4));
endmodule

module RAM_2x2 (
  input  Read___Write,
  input  [1:0] Data_In,
  input  Address_Line,
  input  Clear,
  input  Chip_Select,
  output [1:0] Data_Out
);

  wire clock_1_out, decoder_1_out0, decoder_1_out1, not_1_out;
  wire [1:0] controlled_buffer_1_out, controlled_buffer_2_out, controlled_buffer_3_out, register_1_q,
       register_2_q;

  Decoder decoder_1 (.out0(decoder_1_out0), .out1(decoder_1_out1), .sel(Address_Line), .en(Chip_Select));
  assign controlled_buffer_1_out = Read___Write ? Data_In : 2'bz;  // Controlled_Buffer controlled_buffer_1
  Clock clock_1 (.out(clock_1_out));
  not not_1 (not_1_out, Read___Write);
  Register #(.width(2)) register_1 (
    .D(controlled_buffer_1_out), .en(decoder_1_out0), .Q(register_1_q), .clk(clock_1_out), .clr(Clear));
  Register #(.width(2)) register_2 (
    .D(controlled_buffer_1_out), .en(decoder_1_out1), .Q(register_2_q), .clk(clock_1_out), .clr(Clear));
  assign controlled_buffer_2_out = not_1_out ? register_1_q : 2'bz;  // Controlled_Buffer controlled_buffer_2
  assign controlled_buffer_3_out = not_1_out ? register_2_q : 2'bz;  // Controlled_Buffer controlled_buffer_3
  Multiplexer #(.width(2)) multiplexer_1 (
    .in0(controlled_buffer_2_out), .in1(controlled_buffer_3_out), .out(Data_Out), .sel(Address_Line),
    .en(Chip_Select));
endmodule
