// Logisim project LAB9-ROM.circ as structural Verilog: 2 circuits, main circuit ROM 8 Bit
module ROM_8_Bit (
  input  [7:0] in_1,
  input  in_2,
  output [7:0] out_3
);

  ROM rom_1 (.addr(in_1), .data(out_3), .sel(in_2));
endmodule

module ROM_2X2 (
  input  in_1,
  input  in_2,
  output [1:0] out_3
);

  wire demultiplexer_1_out0, demultiplexer_1_out1;
  wire [1:0] register_1_q, register_2_q;

  Demultiplexer demultiplexer_1 (
    .out0(demultiplexer_1_out0), .out1(demultiplexer_1_out1), .sel(in_1), .en(in_2));  // open: in
  Register #(.width(2)) register_1 (.en(demultiplexer_1_out0), .Q(register_1_q));  // open: D, clk, clr
  Register #(.width(2)) register_2 (.en(demultiplexer_1_out1), .Q(register_2_q));  // open: D, clk, clr
  Multiplexer #(.width(2)) multiplexer_1 (.in0(register_1_q), .in1(register_2_q), .out(out_3), .sel(in_1), .en(in_2));
endmodule
